// Logisim project project.circ as structural Verilog: 5 circuits, main circuit main
// rising
module main (
);

  wire and_1_out, and_2_out, and_3_out, button_1_out, button_2_out, button_3_out, button_4_out, cdm_16_1_p1,
       cdm_16_1_p3, cdm_16_1_p4, cdm_16_1_p5, cdm_16_1_p7, cdm_16_1_p8, cdm_16_1_p9, cdm_16_1_p10,
       cdm_16_1_p11, clk, comparator_1_lt, comparator_2_gt, comparator_3_eq, jIAck, jIRQ, not_1_out;
  wire [1:0] joystick_1_x, joystick_1_y;
  wire [5:0] cdm_16_1_p2;
  wire [15:0] cdm_16_1_p12, cdm_16_1_p13, cdm_16_1_p14, controlled_buffer_1_out, joy, subtractor_1_out;
  wire [31:0] video_adapter_1_o1, video_adapter_1_o2, video_adapter_1_o3, video_adapter_1_o4,
       video_adapter_1_o5, video_adapter_1_o6, video_adapter_1_o7, video_adapter_1_o8, video_adapter_1_o9,
       video_adapter_1_o10, video_adapter_1_o11, video_adapter_1_o12, video_adapter_1_o13,
       video_adapter_1_o14, video_adapter_1_o15, video_adapter_1_o16, video_adapter_1_o17,
       video_adapter_1_o18, video_adapter_1_o19, video_adapter_1_o20, video_adapter_1_o21,
       video_adapter_1_o22, video_adapter_1_o23, video_adapter_1_o24, video_adapter_1_o25,
       video_adapter_1_o26, video_adapter_1_o27, video_adapter_1_o28, video_adapter_1_o29,
       video_adapter_1_o30, video_adapter_1_o31, video_adapter_1_o32;

  Clock clock_1 (.out(clk));
  // Probe on cdm_16_1_p5
  // Probe on cdm_16_1_p4
  // CdM_16 cdm_16_1: pin names not known; wires that end beside it: cdm_16_1_p1, cdm_16_1_p2, cdm_16_1_p3, cdm_16_1_p4, cdm_16_1_p5, clk, cdm_16_1_p7, cdm_16_1_p8, cdm_16_1_p9, cdm_16_1_p10, cdm_16_1_p11, cdm_16_1_p12, cdm_16_1_p13, cdm_16_1_p14
  interrupt_arbiter interrupt_arbiter_1 (
    .IRQ_out(cdm_16_1_p1), .vec_out(cdm_16_1_p2), .IAck_out(cdm_16_1_p3), .IRQ_1(jIRQ), .vec_1(6'b000101),
    .IAck_1(jIAck), .clk(clk));  // open: IRQ_2, vec_2, IAck_2
  // Probe on cdm_16_1_p8
  // Probe on cdm_16_1_p7
  Comparator #(.width(16), .mode("unsigned")) comparator_1 (
    .a(cdm_16_1_p12), .b(16'h101), .lt(comparator_1_lt));  // open: gt, eq
  Comparator #(.width(16), .mode("unsigned")) comparator_2 (
    .a(cdm_16_1_p12), .b(16'h7f), .gt(comparator_2_gt));  // open: eq, lt
  Comparator #(.width(16), .mode("unsigned")) comparator_3 (
    .a(cdm_16_1_p12), .b(16'h102), .eq(comparator_3_eq));  // open: gt, lt
  and and_1 (and_1_out, ~and_3_out, cdm_16_1_p9);  // AND_Gate
  and and_2 (and_2_out, comparator_1_lt, comparator_2_gt, cdm_16_1_p9, ~cdm_16_1_p10);  // AND_Gate
  and and_3 (and_3_out, comparator_3_eq, cdm_16_1_p10);
  assign controlled_buffer_1_out = and_3_out ? joy : 16'bz;  // Controlled_Buffer controlled_buffer_1
  // RAM ram_1: pin names not known; wires that end beside it: cdm_16_1_p12, cdm_16_1_p11, and_1_out, clk, cdm_16_1_p10, controlled_buffer_1_out
  not not_1 (not_1_out, cdm_16_1_p10);
  assign controlled_buffer_1_out = not_1_out ? cdm_16_1_p13 : 16'bz;  // Controlled_Buffer controlled_buffer_2
  assign cdm_16_1_p14 = cdm_16_1_p10 ? controlled_buffer_1_out : 16'bz;  // Controlled_Buffer controlled_buffer_3
  Subtractor #(.width(16)) subtractor_1 (.a(cdm_16_1_p12), .b(16'h80), .out(subtractor_1_out));  // open: bin, bout
  DotMatrix #(.inputtype("row"), .matrixcols(32), .matrixrows(32)) dotmatrix_1 (
    .row0(video_adapter_1_o1), .row1(video_adapter_1_o2), .row2(video_adapter_1_o3),
    .row3(video_adapter_1_o4), .row4(video_adapter_1_o5), .row5(video_adapter_1_o6),
    .row6(video_adapter_1_o7), .row7(video_adapter_1_o8), .row8(video_adapter_1_o9),
    .row9(video_adapter_1_o10), .row10(video_adapter_1_o11), .row11(video_adapter_1_o12),
    .row12(video_adapter_1_o13), .row13(video_adapter_1_o14), .row14(video_adapter_1_o15),
    .row15(video_adapter_1_o16), .row16(video_adapter_1_o17), .row17(video_adapter_1_o18),
    .row18(video_adapter_1_o19), .row19(video_adapter_1_o20), .row20(video_adapter_1_o21),
    .row21(video_adapter_1_o22), .row22(video_adapter_1_o23), .row23(video_adapter_1_o24),
    .row24(video_adapter_1_o25), .row25(video_adapter_1_o26), .row26(video_adapter_1_o27),
    .row27(video_adapter_1_o28), .row28(video_adapter_1_o29), .row29(video_adapter_1_o30),
    .row30(video_adapter_1_o31), .row31(video_adapter_1_o32));
  video_adapter video_adapter_1 (
    .in(controlled_buffer_1_out), .clk(clk), .o1(video_adapter_1_o1), .o2(video_adapter_1_o2),
    .o3(video_adapter_1_o3), .o4(video_adapter_1_o4), .o5(video_adapter_1_o5), .o6(video_adapter_1_o6),
    .o7(video_adapter_1_o7), .o8(video_adapter_1_o8), .o9(video_adapter_1_o9), .o10(video_adapter_1_o10),
    .o11(video_adapter_1_o11), .o12(video_adapter_1_o12), .o13(video_adapter_1_o13),
    .o14(video_adapter_1_o14), .o15(video_adapter_1_o15), .o16(video_adapter_1_o16),
    .o17(video_adapter_1_o17), .o18(video_adapter_1_o18), .o19(video_adapter_1_o19),
    .o20(video_adapter_1_o20), .o21(video_adapter_1_o21), .o22(video_adapter_1_o22),
    .o23(video_adapter_1_o23), .o24(video_adapter_1_o24), .o25(video_adapter_1_o25),
    .o26(video_adapter_1_o26), .o27(video_adapter_1_o27), .o28(video_adapter_1_o28),
    .o29(video_adapter_1_o29), .o30(video_adapter_1_o30), .o31(video_adapter_1_o31),
    .o32(video_adapter_1_o32), .addr(subtractor_1_out), .enable(and_2_out));
  Button button_1 (.out(button_1_out));
  Joystick #(.bits(2)) joystick_1 (.x(joystick_1_x), .y(joystick_1_y));
  gamepad gamepad_1 (
    .data(joy), .joy({joystick_1_y, joystick_1_x}), .B(button_3_out), .A(button_4_out), .R(button_2_out),
    .IAck(jIAck), .clk(clk), .IRQ(jIRQ), .L(button_1_out));
  Button button_2 (.out(button_2_out));
  Button button_3 (.out(button_3_out));
  Button button_4 (.out(button_4_out));
endmodule

module interrupt_arbiter (
  input  IRQ_2,
  input  [5:0] vec_2,
  input  IAck_out,
  input  IRQ_1,
  input  [5:0] vec_1,
  input  clk,
  output IRQ_out,
  output [5:0] vec_out,
  output IAck_2,
  output IAck_1
);

  wire and_2_out, and_3_out, and_4_out, and_5_out, and_7_out, and_8_out, d_ff_1_q, d_ff_2_q, or_1_out,
       or_2_out;

  and and_1 (IAck_2, d_ff_1_q, IAck_out);
  and and_2 (and_2_out, IRQ_2, ~IRQ_1, ~d_ff_2_q);  // AND_Gate
  and and_3 (and_3_out, d_ff_1_q, IAck_out);
  and and_4 (and_4_out, ~d_ff_1_q, IRQ_1);  // AND_Gate
  and and_5 (and_5_out, d_ff_2_q, IAck_out);
  and and_6 (IAck_1, IAck_out, d_ff_2_q);
  or or_1 (or_1_out, and_2_out, and_3_out);
  or or_2 (or_2_out, and_4_out, and_5_out);
  D_Flip_Flop d_ff_1 (.clk(clk), .D(or_1_out), .Q(d_ff_1_q));  // open: Qn, preset, en, reset
  D_Flip_Flop d_ff_2 (.clk(clk), .D(or_2_out), .Q(d_ff_2_q));  // open: Qn, preset, en, reset
  and and_7 (and_7_out, d_ff_1_q, IAck_out);
  assign vec_out = and_7_out ? vec_2 : 6'bz;  // Controlled_Buffer controlled_buffer_1
  and and_8 (and_8_out, d_ff_2_q, IAck_out);
  assign vec_out = and_8_out ? vec_1 : 6'bz;  // Controlled_Buffer controlled_buffer_2
  Pull_Resistor pull_resistor_1 (.node(IRQ_out));
  assign IRQ_out = d_ff_1_q ? IRQ_2 : 1'bz;  // Controlled_Buffer controlled_buffer_3
  assign IRQ_out = d_ff_2_q ? IRQ_1 : 1'bz;  // Controlled_Buffer controlled_buffer_4
endmodule

module gamepad (
  input  IAck,
  input  clk,
  input  [3:0] joy,
  input  R,
  input  L,
  input  B,
  input  A,
  output [15:0] data,
  output IRQ
);

  wire and_5_out, comparator_1_eq;
  wire [5:2] and_3_out;
  wire [15:0] register_1_q;

  and and_1 (and_3_out[4], joy[0], joy[1]);
  and and_2 (and_3_out[5], joy[0], ~joy[1]);  // AND_Gate
  and and_3 (and_3_out[2], joy[2], joy[3]);
  and and_4 (and_3_out[3], joy[2], ~joy[3]);  // AND_Gate
  Register #(.width(16)) register_1 (
    .D({{8{1'b0}}, L, R, and_3_out, B, A}), .en(and_5_out), .Q(register_1_q), .clk(clk));  // open: clr
  and and_5 (and_5_out, ~IAck, comparator_1_eq);  // AND_Gate
  Register #(.width(16), .trigger("falling")) register_2 (
    .D(register_1_q), .en(IAck), .Q(data), .clk(clk));  // open: clr
  Comparator #(.width(16), .mode("unsigned")) comparator_1 (
    .a(data), .b(register_1_q), .eq(comparator_1_eq));  // open: gt, lt
  not not_1 (IRQ, comparator_1_eq);
endmodule

module video_adapter (
  input  [15:0] addr,
  input  [15:0] in,
  input  enable,
  input  clk,
  output [31:0] o1,
  output [31:0] o2,
  output [31:0] o3,
  output [31:0] o4,
  output [31:0] o5,
  output [31:0] o6,
  output [31:0] o7,
  output [31:0] o8,
  output [31:0] o9,
  output [31:0] o10,
  output [31:0] o11,
  output [31:0] o12,
  output [31:0] o13,
  output [31:0] o14,
  output [31:0] o15,
  output [31:0] o16,
  output [31:0] o17,
  output [31:0] o18,
  output [31:0] o19,
  output [31:0] o20,
  output [31:0] o21,
  output [31:0] o22,
  output [31:0] o23,
  output [31:0] o24,
  output [31:0] o25,
  output [31:0] o26,
  output [31:0] o27,
  output [31:0] o28,
  output [31:0] o29,
  output [31:0] o30,
  output [31:0] o31,
  output [31:0] o32
);

  wire and_1_out, and_2_out, and_3_out, demultiplexer_1_out0, demultiplexer_1_out1, demultiplexer_1_out2,
       demultiplexer_1_out3, demultiplexer_1_out4, demultiplexer_1_out5, demultiplexer_1_out6,
       demultiplexer_1_out7, demultiplexer_1_out8, demultiplexer_1_out9, demultiplexer_1_out10,
       demultiplexer_1_out11, demultiplexer_1_out12, demultiplexer_1_out13, demultiplexer_1_out14,
       demultiplexer_1_out15, demultiplexer_1_out16, demultiplexer_1_out17, demultiplexer_1_out18,
       demultiplexer_1_out19, demultiplexer_1_out20, demultiplexer_1_out21, demultiplexer_1_out22,
       demultiplexer_1_out23, demultiplexer_1_out24, demultiplexer_1_out25, demultiplexer_1_out26,
       demultiplexer_1_out27, demultiplexer_1_out28, demultiplexer_1_out29, demultiplexer_1_out30,
       demultiplexer_1_out31, demultiplexer_2_out0, demultiplexer_2_out1, demultiplexer_2_out2,
       demultiplexer_2_out3, demultiplexer_2_out4, demultiplexer_2_out5, demultiplexer_2_out6,
       demultiplexer_2_out7, demultiplexer_2_out8, demultiplexer_2_out9, demultiplexer_2_out10,
       demultiplexer_2_out11, demultiplexer_2_out12, demultiplexer_2_out13, demultiplexer_2_out14,
       demultiplexer_2_out15, demultiplexer_2_out16, demultiplexer_2_out17, demultiplexer_2_out18,
       demultiplexer_2_out19, demultiplexer_2_out20, demultiplexer_2_out21, demultiplexer_2_out22,
       demultiplexer_2_out23, demultiplexer_2_out24, demultiplexer_2_out25, demultiplexer_2_out26,
       demultiplexer_2_out27, demultiplexer_2_out28, demultiplexer_2_out29, demultiplexer_2_out30,
       demultiplexer_2_out31, not_1_out, not_2_out, pull_resistor_1_node, stable_clock_1_p1,
       stable_clock_1_p3;
  wire [15:0] register_1_q, register_2_q;
  wire [31:0] demultiplexer_3_out31;

  and and_1 (and_1_out, ~addr[7], enable);  // AND_Gate
  Demultiplexer #(.select(5), .disabled(0), .enable("false")) demultiplexer_1 (
    .out0(demultiplexer_1_out0), .out1(demultiplexer_1_out1), .out2(demultiplexer_1_out2),
    .out3(demultiplexer_1_out3), .out4(demultiplexer_1_out4), .out5(demultiplexer_1_out5),
    .out6(demultiplexer_1_out6), .out7(demultiplexer_1_out7), .out8(demultiplexer_1_out8),
    .out9(demultiplexer_1_out9), .out10(demultiplexer_1_out10), .out11(demultiplexer_1_out11),
    .out12(demultiplexer_1_out12), .out13(demultiplexer_1_out13), .out14(demultiplexer_1_out14),
    .out15(demultiplexer_1_out15), .out16(demultiplexer_1_out16), .out17(demultiplexer_1_out17),
    .out18(demultiplexer_1_out18), .out19(demultiplexer_1_out19), .out20(demultiplexer_1_out20),
    .out21(demultiplexer_1_out21), .out22(demultiplexer_1_out22), .out23(demultiplexer_1_out23),
    .out24(demultiplexer_1_out24), .out25(demultiplexer_1_out25), .out26(demultiplexer_1_out26),
    .out27(demultiplexer_1_out27), .out28(demultiplexer_1_out28), .out29(demultiplexer_1_out29),
    .out30(demultiplexer_1_out30), .out31(demultiplexer_1_out31), .in(and_1_out), .sel(addr[6:2]));
  not not_1 (not_1_out, addr[1]);
  row_register row_register_1 (.in(in), .half(not_1_out), .enable(demultiplexer_1_out0), .in_2(o1), .clk(clk));
  row_register row_register_2 (.in(in), .half(not_1_out), .enable(demultiplexer_1_out1), .in_2(o2), .clk(clk));
  row_register row_register_3 (.in(in), .half(not_1_out), .enable(demultiplexer_1_out2), .in_2(o3), .clk(clk));
  row_register row_register_4 (.in(in), .half(not_1_out), .enable(demultiplexer_1_out3), .in_2(o4), .clk(clk));
  row_register row_register_5 (.in(in), .half(not_1_out), .enable(demultiplexer_1_out4), .in_2(o5), .clk(clk));
  row_register row_register_6 (.in(in), .half(not_1_out), .enable(demultiplexer_1_out5), .in_2(o6), .clk(clk));
  row_register row_register_7 (.in(in), .half(not_1_out), .enable(demultiplexer_1_out6), .in_2(o7), .clk(clk));
  row_register row_register_8 (.in(in), .half(not_1_out), .enable(demultiplexer_1_out7), .in_2(o8), .clk(clk));
  row_register row_register_9 (.in(in), .half(not_1_out), .enable(demultiplexer_1_out8), .in_2(o9), .clk(clk));
  row_register row_register_10 (.in(in), .half(not_1_out), .enable(demultiplexer_1_out9), .in_2(o10), .clk(clk));
  row_register row_register_11 (.in(in), .half(not_1_out), .enable(demultiplexer_1_out10), .in_2(o11), .clk(clk));
  row_register row_register_12 (.in(in), .half(not_1_out), .enable(demultiplexer_1_out11), .in_2(o12), .clk(clk));
  row_register row_register_13 (.in(in), .half(not_1_out), .enable(demultiplexer_1_out12), .in_2(o13), .clk(clk));
  row_register row_register_14 (.in(in), .half(not_1_out), .enable(demultiplexer_1_out13), .in_2(o14), .clk(clk));
  row_register row_register_15 (.in(in), .half(not_1_out), .enable(demultiplexer_1_out14), .in_2(o15), .clk(clk));
  row_register row_register_16 (.in(in), .half(not_1_out), .enable(demultiplexer_1_out15), .in_2(o16), .clk(clk));
  row_register row_register_17 (.in(in), .half(not_1_out), .enable(demultiplexer_1_out16), .in_2(o17), .clk(clk));
  row_register row_register_18 (.in(in), .half(not_1_out), .enable(demultiplexer_1_out17), .in_2(o18), .clk(clk));
  row_register row_register_19 (.in(in), .half(not_1_out), .enable(demultiplexer_1_out18), .in_2(o19), .clk(clk));
  row_register row_register_20 (.in(in), .half(not_1_out), .enable(demultiplexer_1_out19), .in_2(o20), .clk(clk));
  row_register row_register_21 (.in(in), .half(not_1_out), .enable(demultiplexer_1_out20), .in_2(o21), .clk(clk));
  row_register row_register_22 (.in(in), .half(not_1_out), .enable(demultiplexer_1_out21), .in_2(o22), .clk(clk));
  row_register row_register_23 (.in(in), .half(not_1_out), .enable(demultiplexer_1_out22), .in_2(o23), .clk(clk));
  row_register row_register_24 (.in(in), .half(not_1_out), .enable(demultiplexer_1_out23), .in_2(o24), .clk(clk));
  row_register row_register_25 (.in(in), .half(not_1_out), .enable(demultiplexer_1_out24), .in_2(o25), .clk(clk));
  row_register row_register_26 (.in(in), .half(not_1_out), .enable(demultiplexer_1_out25), .in_2(o26), .clk(clk));
  row_register row_register_27 (.in(in), .half(not_1_out), .enable(demultiplexer_1_out26), .in_2(o27), .clk(clk));
  row_register row_register_28 (.in(in), .half(not_1_out), .enable(demultiplexer_1_out27), .in_2(o28), .clk(clk));
  row_register row_register_29 (.in(in), .half(not_1_out), .enable(demultiplexer_1_out28), .in_2(o29), .clk(clk));
  row_register row_register_30 (.in(in), .half(not_1_out), .enable(demultiplexer_1_out29), .in_2(o30), .clk(clk));
  row_register row_register_31 (.in(in), .half(not_1_out), .enable(demultiplexer_1_out30), .in_2(o31), .clk(clk));
  row_register row_register_32 (.in(in), .half(not_1_out), .enable(demultiplexer_1_out31), .in_2(o32), .clk(clk));
  and and_2 (and_2_out, enable, addr[7]);
  Register #(.width(16)) register_1 (.D(in), .en(and_2_out), .Q(register_1_q), .clk(clk));  // open: clr
  assign o1 = demultiplexer_2_out0 ? demultiplexer_3_out31 : 32'bz;  // Controlled_Buffer controlled_buffer_1
  assign o2 = demultiplexer_2_out1 ? demultiplexer_3_out31 : 32'bz;  // Controlled_Buffer controlled_buffer_2
  Register #(.width(16), .trigger("falling")) register_2 (
    .D(register_1_q), .Q(register_2_q), .clk(clk));  // open: en, clr
  Demultiplexer #(.select(5), .enable("false")) demultiplexer_2 (
    .out0(demultiplexer_2_out0), .out1(demultiplexer_2_out1), .out2(demultiplexer_2_out2),
    .out3(demultiplexer_2_out3), .out4(demultiplexer_2_out4), .out5(demultiplexer_2_out5),
    .out6(demultiplexer_2_out6), .out7(demultiplexer_2_out7), .out8(demultiplexer_2_out8),
    .out9(demultiplexer_2_out9), .out10(demultiplexer_2_out10), .out11(demultiplexer_2_out11),
    .out12(demultiplexer_2_out12), .out13(demultiplexer_2_out13), .out14(demultiplexer_2_out14),
    .out15(demultiplexer_2_out15), .out16(demultiplexer_2_out16), .out17(demultiplexer_2_out17),
    .out18(demultiplexer_2_out18), .out19(demultiplexer_2_out19), .out20(demultiplexer_2_out20),
    .out21(demultiplexer_2_out21), .out22(demultiplexer_2_out22), .out23(demultiplexer_2_out23),
    .out24(demultiplexer_2_out24), .out25(demultiplexer_2_out25), .out26(demultiplexer_2_out26),
    .out27(demultiplexer_2_out27), .out28(demultiplexer_2_out28), .out29(demultiplexer_2_out29),
    .out30(demultiplexer_2_out30), .out31(demultiplexer_2_out31), .in(1'b1), .sel(register_1_q[9:5]));
  assign o3 = demultiplexer_2_out2 ? demultiplexer_3_out31 : 32'bz;  // Controlled_Buffer controlled_buffer_3
  assign o4 = demultiplexer_2_out3 ? demultiplexer_3_out31 : 32'bz;  // Controlled_Buffer controlled_buffer_4
  // stable_clock stable_clock_1: pin names not known; wires that end beside it: stable_clock_1_p1, clk, stable_clock_1_p3
  Comparator #(.width(16), .mode("unsigned")) comparator_1 (
    .a(register_1_q), .b(register_2_q), .eq(stable_clock_1_p1));  // open: gt, lt
  assign o5 = demultiplexer_2_out4 ? demultiplexer_3_out31 : 32'bz;  // Controlled_Buffer controlled_buffer_5
  assign o6 = demultiplexer_2_out5 ? demultiplexer_3_out31 : 32'bz;  // Controlled_Buffer controlled_buffer_6
  not not_2 (not_2_out, stable_clock_1_p3);
  assign o8 = demultiplexer_2_out7 ? demultiplexer_3_out31 : 32'bz;  // Controlled_Buffer controlled_buffer_7
  assign o7 = demultiplexer_2_out6 ? demultiplexer_3_out31 : 32'bz;  // Controlled_Buffer controlled_buffer_8
  and and_3 (and_3_out, ~register_1_q[15], not_2_out);  // AND_Gate
  assign o9 = demultiplexer_2_out8 ? demultiplexer_3_out31 : 32'bz;  // Controlled_Buffer controlled_buffer_9
  assign o10 = demultiplexer_2_out9 ? demultiplexer_3_out31 : 32'bz;  // Controlled_Buffer controlled_buffer_10
  assign o12 = demultiplexer_2_out11 ? demultiplexer_3_out31 : 32'bz;  // Controlled_Buffer controlled_buffer_11
  assign o11 = demultiplexer_2_out10 ? demultiplexer_3_out31 : 32'bz;  // Controlled_Buffer controlled_buffer_12
  assign o13 = demultiplexer_2_out12 ? demultiplexer_3_out31 : 32'bz;  // Controlled_Buffer controlled_buffer_13
  assign o14 = demultiplexer_2_out13 ? demultiplexer_3_out31 : 32'bz;  // Controlled_Buffer controlled_buffer_14
  assign o15 = demultiplexer_2_out14 ? demultiplexer_3_out31 : 32'bz;  // Controlled_Buffer controlled_buffer_15
  assign o16 = demultiplexer_2_out15 ? demultiplexer_3_out31 : 32'bz;  // Controlled_Buffer controlled_buffer_16
  assign o17 = demultiplexer_2_out16 ? demultiplexer_3_out31 : 32'bz;  // Controlled_Buffer controlled_buffer_17
  assign o18 = demultiplexer_2_out17 ? demultiplexer_3_out31 : 32'bz;  // Controlled_Buffer controlled_buffer_18
  assign o20 = demultiplexer_2_out19 ? demultiplexer_3_out31 : 32'bz;  // Controlled_Buffer controlled_buffer_19
  assign o19 = demultiplexer_2_out18 ? demultiplexer_3_out31 : 32'bz;  // Controlled_Buffer controlled_buffer_20
  assign o22 = demultiplexer_2_out21 ? demultiplexer_3_out31 : 32'bz;  // Controlled_Buffer controlled_buffer_21
  assign o21 = demultiplexer_2_out20 ? demultiplexer_3_out31 : 32'bz;  // Controlled_Buffer controlled_buffer_22
  assign o24 = demultiplexer_2_out23 ? demultiplexer_3_out31 : 32'bz;  // Controlled_Buffer controlled_buffer_23
  assign o23 = demultiplexer_2_out22 ? demultiplexer_3_out31 : 32'bz;  // Controlled_Buffer controlled_buffer_24
  assign o25 = demultiplexer_2_out24 ? demultiplexer_3_out31 : 32'bz;  // Controlled_Buffer controlled_buffer_25
  assign o26 = demultiplexer_2_out25 ? demultiplexer_3_out31 : 32'bz;  // Controlled_Buffer controlled_buffer_26
  assign o28 = demultiplexer_2_out27 ? demultiplexer_3_out31 : 32'bz;  // Controlled_Buffer controlled_buffer_27
  assign o27 = demultiplexer_2_out26 ? demultiplexer_3_out31 : 32'bz;  // Controlled_Buffer controlled_buffer_28
  assign o30 = demultiplexer_2_out29 ? demultiplexer_3_out31 : 32'bz;  // Controlled_Buffer controlled_buffer_29
  assign o29 = demultiplexer_2_out28 ? demultiplexer_3_out31 : 32'bz;  // Controlled_Buffer controlled_buffer_30
  assign o32 = demultiplexer_2_out31 ? demultiplexer_3_out31 : 32'bz;  // Controlled_Buffer controlled_buffer_31
  assign o31 = demultiplexer_2_out30 ? demultiplexer_3_out31 : 32'bz;  // Controlled_Buffer controlled_buffer_32
  Demultiplexer #(.select(5), .tristate("true")) demultiplexer_3 (
    .out0(demultiplexer_3_out31[31]), .out1(demultiplexer_3_out31[30]), .out2(demultiplexer_3_out31[29]),
    .out3(demultiplexer_3_out31[28]), .out4(demultiplexer_3_out31[27]), .out5(demultiplexer_3_out31[26]),
    .out6(demultiplexer_3_out31[25]), .out7(demultiplexer_3_out31[24]), .out8(demultiplexer_3_out31[23]),
    .out9(demultiplexer_3_out31[22]), .out10(demultiplexer_3_out31[21]), .out11(demultiplexer_3_out31[20]),
    .out12(demultiplexer_3_out31[19]), .out13(demultiplexer_3_out31[18]), .out14(demultiplexer_3_out31[17]),
    .out15(demultiplexer_3_out31[16]), .out16(demultiplexer_3_out31[15]), .out17(demultiplexer_3_out31[14]),
    .out18(demultiplexer_3_out31[13]), .out19(demultiplexer_3_out31[12]), .out20(demultiplexer_3_out31[11]),
    .out21(demultiplexer_3_out31[10]), .out22(demultiplexer_3_out31[9]), .out23(demultiplexer_3_out31[8]),
    .out24(demultiplexer_3_out31[7]), .out25(demultiplexer_3_out31[6]), .out26(demultiplexer_3_out31[5]),
    .out27(demultiplexer_3_out31[4]), .out28(demultiplexer_3_out31[3]), .out29(demultiplexer_3_out31[2]),
    .out30(demultiplexer_3_out31[1]), .out31(demultiplexer_3_out31[0]), .in(pull_resistor_1_node),
    .sel(register_1_q[4:0]), .en(and_3_out));
  Pull_Resistor #(.pull("X")) pull_resistor_1 (.node(pull_resistor_1_node));

  // Other names for the same wires on the sheet: cur = addr[7]
endmodule

module row_register (
  input  [15:0] in,
  input  half,
  input  enable,
  input  clk,
  output [31:0] in_2
);

  wire and_1_out, and_2_out;

  and and_1 (and_1_out, enable, ~half);  // AND_Gate
  and and_2 (and_2_out, enable, half);
  Register #(.width(16)) register_1 (.D(in), .en(and_1_out), .Q(in_2[15:0]), .clk(clk));  // open: clr
  Register #(.width(16)) register_2 (.D(in), .en(and_2_out), .Q(in_2[31:16]), .clk(clk));  // open: clr
endmodule
